# Fritzing sketch clap_relay (saved by Fritzing 0.9.3b)
breadboards: 1

parts:
  Часть1 = Arduino Leonardo (Rev3b)
  Part1 = KY-019 5V Relay Module [package="Breakout board"]
  FC-1 = Sound Sensor
  LED1 = smd LED [color="Red (633nm)" package="0805 [SMD]"]
  R1 = Resistor [tolerance=±5% resistance=220 package=THT]

nets:
  N1: Часть1.D4/A6, Part1.S
  N2: Часть1.D5_PWM, FC-1.OUT
  5V: Часть1.5V, Part1.+, FC-1.VCC
  GND: Часть1.GND, Part1.-, FC-1.GND
  N3: Part1.NC, R1.Pin_1
  N4: Part1.Common, LED1.cathode
  N5: LED1.anode, R1.Pin_0

custom parts:
  KY-019 5V Relay Module: KY-019 5V Relay module, used to control AC circuits.
